// Logisim project cpu.circ as structural Verilog: 1 circuit, main circuit main
module main (
  input  CLK_RUN,
  input  CLK_HLT,
  input  [7:0] in_3,
  input  [15:0] in_4,
  input  in_5,
  input  in_6,
  input  IP_HI_TO_DATA,
  input  IP_LO_TO_DATA,
  input  A_TO_DATA,
  input  DATA_TO_A,
  input  DATA_TO_IP_HI,
  input  DATA_TO_IP_LO,
  input  IP_TO_ADDR,
  input  A_TO_X,
  input  IP_INC,
  input  Z_TO_DATA,
  input  ADDR_TO_IP,
  input  SUB,
  input  DATA_TO_MAR_HI,
  input  DATA_TO_MAR_LO,
  input  MAR_INC,
  input  ADDR_TO_MAR,
  input  FLAGS,
  input  MDR_TO_DATA,
  input  DATA_TO_MDR,
  input  H_TO_DATA,
  input  L_TO_DATA,
  input  DATA_TO_Y,
  input  DATA_TO_H,
  input  DATA_TO_L,
  input  HL_TO_ADDR,
  input  B_TO_DATA,
  input  DATA_TO_B,
  input  ADDR_TO_HL,
  input  C_TO_DATA,
  input  DATA_TO_C,
  input  TH_TO_DATA,
  input  TL_TO_DATA,
  input  D_TO_DATA,
  input  DATA_TO_D,
  input  DATA_TO_TH,
  input  DATA_TO_TL,
  input  T_TO_ADDR,
  input  SP_HI_TO_DATA,
  input  SP_LO_TO_DATA,
  input  DATA_TO_SP_HI,
  input  DATA_TO_SP_LO,
  input  SP_TO_ADDR,
  input  SP_DEC,
  input  SP_INC,
  input  ADDR_TO_SP,
  output [7:0] out_52,
  output [15:0] out_53,
  output [15:0] out_54,
  output [7:0] out_55,
  output [7:0] out_56,
  output [15:0] out_57,
  output [7:0] out_58,
  output [7:0] out_59,
  output [7:0] out_60,
  output [7:0] out_61,
  output [7:0] out_62,
  output [15:0] out_63,
  output [7:0] out_64,
  output [7:0] out_65,
  output [7:0] out_66,
  output [7:0] out_67,
  output [7:0] out_68,
  output [15:0] out_69,
  output [7:0] out_70,
  output [15:0] out_71
);

  wire adder_1_cout, and_1_out, and_2_out, CLK, CLK_STEP_out, clock_1_out, minus_CLK, nor_1_out, nor_2_out,
       nor_3_out, nor_4_out, nor_5_out, nor_6_out, nor_7_out, nor_8_out, nor_9_out, not_1_out, not_2_out,
       not_3_out, not_5_out, not_6_out, or_1_out, or_2_out, or_3_out, or_4_out, or_5_out, or_6_out, or_7_out,
       or_8_out, RST;
  wire [7:0] bit_extender_1_out, controlled_buffer_8_out, controlled_buffer_9_out, controlled_buffer_13_out,
       controlled_buffer_15_out, controlled_buffer_17_out, controlled_buffer_20_out,
       controlled_buffer_22_out, controlled_buffer_25_out, controlled_buffer_28_out,
       controlled_buffer_31_out, xor_1_out;

  nor nor_1 (nor_1_out, out_58[0], out_58[1], out_58[2], out_58[3], out_58[4], out_58[5], out_58[6], out_58[7]);
  D_Flip_Flop d_ff_1 (.clk(CLK), .D(nor_1_out), .Q(out_60[0]), .en(FLAGS), .reset(RST));  // open: Qn, preset
  D_Flip_Flop d_ff_2 (.clk(CLK), .D(adder_1_cout), .Q(out_60[1]), .en(FLAGS), .reset(RST));  // open: Qn, preset
  assign bit_extender_1_out = {{7{SUB}}, SUB};  // Bit_Extender bit_extender_1
  Register register_1 (.D(out_52), .en(DATA_TO_A), .Q(out_55), .clk(CLK));  // open: clr
  assign out_52 = A_TO_DATA ? out_55 : 8'bz;  // Controlled_Buffer controlled_buffer_1
  Register register_2 (.D(out_55), .en(A_TO_X), .Q(out_56), .clk(CLK));  // open: clr
  Adder adder_1 (.a(out_56), .b(xor_1_out), .out(out_58), .cin(SUB), .cout(adder_1_cout));
  assign xor_1_out = bit_extender_1_out ^ out_64;  // XOR_Gate xor_1, 8 bits wide
  Register register_3 (.D(out_52), .en(DATA_TO_Y), .Q(out_64), .clk(CLK));  // open: clr
  Register register_4 (.D(out_52), .en(DATA_TO_B), .Q(out_65), .clk(CLK));  // open: clr
  assign out_52 = B_TO_DATA ? out_65 : 8'bz;  // Controlled_Buffer controlled_buffer_2
  assign out_52 = C_TO_DATA ? out_66 : 8'bz;  // Controlled_Buffer controlled_buffer_3
  Register register_5 (.D(out_52), .en(DATA_TO_C), .Q(out_66), .clk(CLK));  // open: clr
  Register register_6 (.D(out_52), .en(DATA_TO_D), .Q(out_70), .clk(CLK));  // open: clr
  assign out_52 = D_TO_DATA ? out_70 : 8'bz;  // Controlled_Buffer controlled_buffer_4
  Button CLK_STEP (.out(CLK_STEP_out));
  Button u_RST (.out(RST));
  Clock clock_1 (.out(clock_1_out));
  not not_1 (not_1_out, CLK_RUN);
  not not_2 (not_2_out, CLK_HLT);
  assign out_52 = in_5 ? in_3 : 8'bz;  // Controlled_Buffer controlled_buffer_5
  assign out_52 = Z_TO_DATA ? out_58 : 8'bz;  // Controlled_Buffer controlled_buffer_6
  and and_1 (and_1_out, clock_1_out, CLK_RUN);
  or or_1 (or_1_out, and_1_out, and_2_out);
  and and_2 (and_2_out, not_1_out, CLK_STEP_out);
  assign out_52 = IP_LO_TO_DATA ? out_54[7:0] : 8'bz;  // Controlled_Buffer controlled_buffer_7
  assign controlled_buffer_8_out = DATA_TO_IP_LO ? out_52 : 8'bz;  // Controlled_Buffer controlled_buffer_8
  assign controlled_buffer_9_out = DATA_TO_MAR_LO ? out_52 : 8'bz;  // Controlled_Buffer controlled_buffer_9
  assign out_59 = DATA_TO_MDR ? out_52 : 8'bz;  // Controlled_Buffer controlled_buffer_10
  assign out_52 = MDR_TO_DATA ? out_59 : 8'bz;  // Controlled_Buffer controlled_buffer_11
  assign out_52 = L_TO_DATA ? out_62 : 8'bz;  // Controlled_Buffer controlled_buffer_12
  assign controlled_buffer_13_out = DATA_TO_L ? out_52 : 8'bz;  // Controlled_Buffer controlled_buffer_13
  assign out_52 = TL_TO_DATA ? out_68 : 8'bz;  // Controlled_Buffer controlled_buffer_14
  not not_3 (not_3_out, DATA_TO_TL);
  assign controlled_buffer_15_out = DATA_TO_TL ? out_52 : 8'bz;  // Controlled_Buffer controlled_buffer_15
  assign out_52 = SP_LO_TO_DATA ? out_71[7:0] : 8'bz;  // Controlled_Buffer controlled_buffer_16
  assign controlled_buffer_17_out = DATA_TO_SP_LO ? out_52 : 8'bz;  // Controlled_Buffer controlled_buffer_17
  and and_3 (CLK, or_1_out, not_2_out);
  not not_4 (minus_CLK, CLK);
  assign out_52 = IP_HI_TO_DATA ? out_54[15:8] : 8'bz;  // Controlled_Buffer controlled_buffer_18
  nor nor_2 (nor_2_out, DATA_TO_IP_LO, ADDR_TO_IP);
  assign controlled_buffer_8_out = nor_2_out ? out_54[7:0] : 8'bz;  // Controlled_Buffer controlled_buffer_19
  assign controlled_buffer_20_out = DATA_TO_IP_HI ? out_52 : 8'bz;  // Controlled_Buffer controlled_buffer_20
  nor nor_3 (nor_3_out, DATA_TO_MAR_LO, ADDR_TO_MAR);
  assign controlled_buffer_9_out = nor_3_out ? out_57[7:0] : 8'bz;  // Controlled_Buffer controlled_buffer_21
  assign controlled_buffer_22_out = DATA_TO_MAR_HI ? out_52 : 8'bz;  // Controlled_Buffer controlled_buffer_22
  not not_5 (not_5_out, DATA_TO_MDR);
  assign out_52 = H_TO_DATA ? out_61 : 8'bz;  // Controlled_Buffer controlled_buffer_23
  nor nor_4 (nor_4_out, DATA_TO_L, ADDR_TO_HL);
  assign controlled_buffer_13_out = nor_4_out ? out_62 : 8'bz;  // Controlled_Buffer controlled_buffer_24
  assign controlled_buffer_25_out = DATA_TO_H ? out_52 : 8'bz;  // Controlled_Buffer controlled_buffer_25
  assign out_52 = TH_TO_DATA ? out_67 : 8'bz;  // Controlled_Buffer controlled_buffer_26
  not not_6 (not_6_out, DATA_TO_TH);
  assign controlled_buffer_15_out = not_3_out ? out_68 : 8'bz;  // Controlled_Buffer controlled_buffer_27
  assign controlled_buffer_28_out = DATA_TO_TH ? out_52 : 8'bz;  // Controlled_Buffer controlled_buffer_28
  or or_2 (or_2_out, DATA_TO_TH, DATA_TO_TL);
  assign out_52 = SP_HI_TO_DATA ? out_71[15:8] : 8'bz;  // Controlled_Buffer controlled_buffer_29
  nor nor_5 (nor_5_out, DATA_TO_SP_LO, ADDR_TO_SP);
  assign controlled_buffer_17_out = nor_5_out ? out_71[7:0] : 8'bz;  // Controlled_Buffer controlled_buffer_30
  assign controlled_buffer_31_out = DATA_TO_SP_HI ? out_52 : 8'bz;  // Controlled_Buffer controlled_buffer_31
  nor nor_6 (nor_6_out, DATA_TO_IP_HI, ADDR_TO_IP);
  assign controlled_buffer_20_out = nor_6_out ? out_54[15:8] : 8'bz;  // Controlled_Buffer controlled_buffer_32
  or or_3 (or_3_out, DATA_TO_IP_HI, DATA_TO_IP_LO, ADDR_TO_IP);
  nor nor_7 (nor_7_out, DATA_TO_MAR_HI, ADDR_TO_MAR);
  assign controlled_buffer_22_out = nor_7_out ? out_57[15:8] : 8'bz;  // Controlled_Buffer controlled_buffer_33
  or or_4 (or_4_out, DATA_TO_MAR_HI, DATA_TO_MAR_LO, ADDR_TO_MAR);
  nor nor_8 (nor_8_out, DATA_TO_H, ADDR_TO_HL);
  assign controlled_buffer_25_out = nor_8_out ? out_61 : 8'bz;  // Controlled_Buffer controlled_buffer_34
  or or_5 (or_5_out, DATA_TO_H, DATA_TO_L, ADDR_TO_HL);
  assign controlled_buffer_28_out = not_6_out ? out_67 : 8'bz;  // Controlled_Buffer controlled_buffer_35
  nor nor_9 (nor_9_out, DATA_TO_SP_HI, ADDR_TO_SP);
  assign controlled_buffer_31_out = nor_9_out ? out_71[15:8] : 8'bz;  // Controlled_Buffer controlled_buffer_36
  or or_6 (or_6_out, DATA_TO_SP_HI, DATA_TO_SP_LO, ADDR_TO_SP);
  Counter #(.width(16), .max('hffff)) counter_1 (
    .load(or_3_out), .D({controlled_buffer_20_out, controlled_buffer_8_out}), .count(IP_INC), .Q(out_54),
    .clk(CLK), .clr(RST));  // open: carry
  Counter #(.width(16), .max('hffff)) counter_2 (
    .load(or_4_out), .D({controlled_buffer_22_out, controlled_buffer_9_out}), .count(MAR_INC), .Q(out_57),
    .clk(CLK));  // open: carry, clr
  Register #(.width(16)) register_7 (
    .D({controlled_buffer_25_out, controlled_buffer_13_out}), .en(or_5_out), .Q({out_61, out_62}), .clk(CLK),
    .clr(RST));
  Register #(.width(16)) register_8 (
    .D({controlled_buffer_28_out, controlled_buffer_15_out}), .en(or_2_out), .Q({out_67, out_68}), .clk(CLK),
    .clr(RST));
  Counter #(.width(16), .max('hffff)) counter_3 (
    .load(or_7_out), .D({controlled_buffer_31_out, controlled_buffer_17_out}), .count(or_8_out), .Q(out_71),
    .clk(CLK), .clr(RST));  // open: carry
  or or_7 (or_7_out, or_6_out, SP_DEC);
  or or_8 (or_8_out, SP_DEC, SP_INC);
  RAM #(.addrWidth(16)) ram_1 (.addr(out_57), .data(out_59), .sel(1'b1), .clk(CLK), .ld(not_5_out));  // open: clr
  assign out_53 = in_6 ? in_4 : 16'bz;  // Controlled_Buffer controlled_buffer_37
  assign out_53 = IP_TO_ADDR ? out_54 : 16'bz;  // Controlled_Buffer controlled_buffer_38
  assign {controlled_buffer_20_out, controlled_buffer_8_out} = ADDR_TO_IP ? out_53 : 16'bz;  // Controlled_Buffer controlled_buffer_39
  assign {controlled_buffer_22_out, controlled_buffer_9_out} = ADDR_TO_MAR ? out_53 : 16'bz;  // Controlled_Buffer controlled_buffer_40
  assign out_53 = HL_TO_ADDR ? {out_61, out_62} : 16'bz;  // Controlled_Buffer controlled_buffer_41
  assign {controlled_buffer_25_out, controlled_buffer_13_out} = ADDR_TO_HL ? out_53 : 16'bz;  // Controlled_Buffer controlled_buffer_42
  assign out_53 = T_TO_ADDR ? {out_67, out_68} : 16'bz;  // Controlled_Buffer controlled_buffer_43
  assign out_53 = SP_TO_ADDR ? out_71 : 16'bz;  // Controlled_Buffer controlled_buffer_44
  assign {controlled_buffer_31_out, controlled_buffer_17_out} = ADDR_TO_SP ? out_53 : 16'bz;  // Controlled_Buffer controlled_buffer_45

  assign out_60[7:2] = {6{1'b0}};
  assign out_63 = {out_61, out_62};
  assign out_69 = {out_67, out_68};

  // Other names for the same wires on the sheet: ZF = out_60[0]; CF = out_60[1]

  // Notes on the sheet:
  //   Adder / Substractor
  //   Flags
  //   A Register
  //   X Register
  //   Y Register
  //   B Register
  //   C Register
  //   D Register
  //   8-Bit Data Bus
  //   Z Register
  //   Clock
  //   TH Register
  //   TL Register
  //   T Register
  //   Instruction Pointer
  //   Memory Address Register
  //   H Register
  //   L Register
  //   HL Register
  //   Stack Pointer
  //   Memory Data Register
  //   16-Bit Address Bus
endmodule
